// Logisim project B1_Group6.circ as structural Verilog: 17 circuits, main circuit main
module main (
  input  [31:0] in_1,
  input  [31:0] in_2,
  output OVERFLOW,
  output UNDERFLOW,
  output [31:0] out_5,
  output out_6,
  output ans_sign,
  output [10:0] ans_exp,
  output [10:0] out_9,
  output [19:0] ans_fraction,
  output [19:0] out_11,
  output [19:0] out_12,
  output [10:0] out_13,
  output out_14
);

  wire firstshift_1_out_5, firstshift_1_out_6;
  wire [10:0] firstpart_1_out_7, firstshift_1_out_4;
  wire [11:0] aftershift_1_out_5;
  wire [31:0] firstpart_1_out_9, firstshift_1_out_3, rounding_1_out_2;

  FirstPart firstpart_1 (
    .in_1(in_1[30:20]), .in_2(in_2[30:20]), .A_sign(in_1[31]), .in_3({4'b0001, in_1[19:0], {8{1'b0}}}),
    .in_5({4'b0001, in_2[19:0], {8{1'b0}}}), .sub(in_2[31]), .out_7(firstpart_1_out_7),
    .out_9(firstpart_1_out_9), .out_8(ans_sign));
  firstShift firstshift_1 (
    .in_1(firstpart_1_out_9), .in_2(firstpart_1_out_7), .out_3(firstshift_1_out_3),
    .out_4(firstshift_1_out_4), .out_5(firstshift_1_out_5), .out_6(firstshift_1_out_6));
  Rounding rounding_1 (.\input (firstshift_1_out_3), .out_2(rounding_1_out_2));
  AfterShift aftershift_1 (
    .in_1(rounding_1_out_2), .in_2(firstshift_1_out_4), .out_5({aftershift_1_out_5, ans_fraction}),
    .out_6(ans_exp), .in_3(firstshift_1_out_5), .in_4(firstshift_1_out_6), .out_8(UNDERFLOW), .out_7(OVERFLOW));

  assign out_5 = {ans_sign, ans_exp, ans_fraction};
  assign out_6 = in_1[31];
  assign out_9 = in_1[30:20];
  assign out_11 = in_1[19:0];
  assign out_12 = in_2[19:0];
  assign out_13 = in_2[30:20];
  assign out_14 = in_2[31];

  // Notes on the sheet:
  //   A sign
  //   A exp
  //   INPUT A
  //   32 bit
  //   INPUT B
  //   32 bit
  //   B exp
  //   B sign
  //   B frac
  //   A frac
  //   OUTPUT 32 bit
endmodule

module FirstPart (
  input  [10:0] in_1,
  input  [10:0] in_2,
  input  [31:0] in_3,
  input  A_sign,
  input  [31:0] in_5,
  input  sub,
  output [10:0] out_7,
  output out_8,
  output [31:0] out_9
);

  wire ic7404_1__2__1y, ic7404_1__4__2y, ic7432_1__3__1y, ic7432_1__6__2y, ic7432_1__8__3y, ic7432_1__11__4y,
       ic7432_2__3__1y, ic7432_2__6__2y, ic7432_2__11__4y, subtractor_1_bout;
  wire [4:0] demux_1_out_3, demux_1_out_4, n32bitmux_3_out_4;
  wire [10:0] n11bitmux_1_out_4;
  wire [30:0] adder_1_out;
  wire [31:0] n32and_1_out_3, n32and_2_out_3, n32bitconverter_1_out_2, n32bitconverter_2_out_2,
       n32bitmux_1_out_4, n32bitmux_2_out_4, negator_1_out, negator_2_out, shifter_1_out, shifter_2_out,
       subtractor_1_out, subtractor_2_out, subtractor_3_out;

  Subtractor #(.width(32)) subtractor_1 (
    .a({{21{1'b0}}, in_1}), .b({{21{1'b0}}, in_2}), .out(subtractor_1_out), .bout(subtractor_1_bout));  // open: bin
  Negator #(.width(32)) negator_1 (.in(subtractor_1_out), .out(negator_1_out));
  Shifter #(.width(32), .shift("lr")) shifter_1 (.in(in_3), .\dist (demux_1_out_4), .out(shifter_1_out));
  Shifter #(.width(32), .shift("lr")) shifter_2 (.in(in_5), .\dist (demux_1_out_3), .out(shifter_2_out));
  IC7404 ic7404_1 (
    ._1__1A(subtractor_1_bout), ._2__1Y(ic7404_1__2__1y), ._3__2A(ic7432_2__3__1y), ._4__2Y(ic7404_1__4__2y));  // open: _5__3A, _6__3Y, _7__GND, _14__Vcc, _13__6A, _12__6Y, _11__5A, _10__5Y, _9__4A, _8__4Y
  _11bitMUX u_11bitmux_1 (
    .in_1(subtractor_1_bout), .in_2(subtractor_1_out[10:0]), .in_3(negator_1_out[10:0]),
    .out_4(n11bitmux_1_out_4));
  Subtractor #(.width(32)) subtractor_2 (.a({32{1'b0}}), .b(shifter_1_out), .out(subtractor_2_out));  // open: bin, bout
  Subtractor #(.width(32)) subtractor_3 (.a({32{1'b0}}), .b(shifter_2_out), .out(subtractor_3_out));  // open: bin, bout
  IC7432 ic7432_1 (
    ._1__1A(n11bitmux_1_out_4[9]), ._2__1B(n11bitmux_1_out_4[8]), ._3__1Y(ic7432_1__3__1y),
    ._4__2A(ic7432_1__3__1y), ._5__2B(n11bitmux_1_out_4[7]), ._6__2Y(ic7432_1__6__2y),
    ._13__4B(n11bitmux_1_out_4[5]), ._12__4A(ic7432_1__8__3y), ._11__4Y(ic7432_1__11__4y),
    ._10__3B(n11bitmux_1_out_4[6]), ._9__3A(ic7432_1__6__2y), ._8__3Y(ic7432_1__8__3y));  // open: _7__GND, _14__Vcc
  DEMUX demux_1 (.in_1(n11bitmux_1_out_4[4:0]), .in_2(subtractor_1_bout), .out_3(demux_1_out_3), .out_4(demux_1_out_4));
  _32bitMUX u_32bitmux_1 (.in_1(A_sign), .in_2(shifter_1_out), .in_3(subtractor_2_out), .out_4(n32bitmux_1_out_4));
  _32bitMUX u_32bitmux_2 (.in_1(sub), .in_2(shifter_2_out), .in_3(subtractor_3_out), .out_4(n32bitmux_2_out_4));
  _32bitConverter u_32bitconverter_1 (.in_1(ic7432_2__6__2y), .out_2(n32bitconverter_1_out_2));
  _32AND u_32and_1 (.in_1(n32bitconverter_2_out_2), .in_2(n32bitmux_1_out_4), .out_3(n32and_1_out_3));
  _32AND u_32and_2 (.in_1(n32bitconverter_1_out_2), .in_2(n32bitmux_2_out_4), .out_3(n32and_2_out_3));
  _32bitConverter u_32bitconverter_2 (.in_1(ic7432_2__11__4y), .out_2(n32bitconverter_2_out_2));
  IC7432 ic7432_2 (
    ._1__1A(n11bitmux_1_out_4[10]), ._2__1B(ic7432_1__11__4y), ._3__1Y(ic7432_2__3__1y),
    ._4__2A(ic7404_1__4__2y), ._5__2B(subtractor_1_bout), ._6__2Y(ic7432_2__6__2y),
    ._13__4B(ic7404_1__2__1y), ._12__4A(ic7404_1__4__2y), ._11__4Y(ic7432_2__11__4y));  // open: _7__GND, _14__Vcc, _10__3B, _9__3A, _8__3Y
  _11bitMUX u_11bitmux_2 (.in_1(subtractor_1_bout), .in_2(in_1), .in_3(in_2), .out_4(out_7));
  Adder #(.width(32)) adder_1 (.a(n32and_1_out_3), .b(n32and_2_out_3), .out({out_8, adder_1_out}));  // open: cin, cout
  Negator #(.width(32)) negator_2 (.in({out_8, adder_1_out}), .out(negator_2_out));
  _32bitMUX u_32bitmux_3 (
    .in_1(out_8), .in_2({out_8, adder_1_out}), .in_3(negator_2_out), .out_4({out_9[26:0], n32bitmux_3_out_4}));

  assign out_9[31:27] = {5{1'b0}};

  // Notes on the sheet:
  //   A exponential
  //   B exponential
  //   A Fraction
  //   B fraction
  //   sub
  //   negator
  //   not
  //   11 mux
  //   B sign
  //   diffrence
  //   sub
  //   demux
  //   32mux
  //   or
  //   MINUS 0 A>B  == 0
  //   MINUS 1 A<B == 1
  //   32mux
  //   32conv
  //   32 and
  //   32conv
  //   32 and
  //   or
  //   exponential
  //   11mux
  //   added two fractions
  //   32 adder
endmodule

module QUADMUX (
  input  in_1,
  input  [3:0] in_2,
  input  [3:0] in_3,
  output [3:0] out_4
);

  IC74157 ic74157_1 (
    ._1__S(in_1), ._2__A1(in_2[0]), ._3__B1(in_3[0]), ._4__Y1(out_4[0]), ._5__A2(in_2[1]), ._6__B2(in_3[1]),
    ._7__Y2(out_4[1]), ._15__G(1'b0), ._14__A4(in_2[3]), ._13__B4(in_3[3]), ._12__Y4(out_4[3]),
    ._11__A3(in_2[2]), ._10__B3(in_3[2]), ._9__Y3(out_4[2]));  // open: _8__GND, _16__Vcc
endmodule

module _32bitMUX (
  input  in_1,
  input  [31:0] in_2,
  input  [31:0] in_3,
  output [31:0] out_4
);

  QUADMUX quadmux_1 (.in_1(in_1), .in_2(in_2[3:0]), .in_3(in_3[3:0]), .out_4(out_4[3:0]));
  QUADMUX quadmux_2 (.in_1(in_1), .in_2(in_2[7:4]), .in_3(in_3[7:4]), .out_4(out_4[7:4]));
  QUADMUX quadmux_3 (.in_1(in_1), .in_2(in_2[11:8]), .in_3(in_3[11:8]), .out_4(out_4[11:8]));
  QUADMUX quadmux_4 (.in_1(in_1), .in_2(in_2[15:12]), .in_3(in_3[15:12]), .out_4(out_4[15:12]));
  QUADMUX quadmux_5 (.in_1(in_1), .in_2(in_2[19:16]), .in_3(in_3[19:16]), .out_4(out_4[19:16]));
  QUADMUX quadmux_6 (.in_1(in_1), .in_2(in_2[23:20]), .in_3(in_3[23:20]), .out_4(out_4[23:20]));
  QUADMUX quadmux_7 (.in_1(in_1), .in_2(in_2[27:24]), .in_3(in_3[27:24]), .out_4(out_4[27:24]));
  QUADMUX quadmux_8 (.in_1(in_1), .in_2(in_2[31:28]), .in_3(in_3[31:28]), .out_4(out_4[31:28]));
endmodule

module _11bitMUX (
  input  in_1,
  input  [10:0] in_2,
  input  [10:0] in_3,
  output [10:0] out_4
);

  wire [3:3] quadmux_3_out_4;

  QUADMUX quadmux_1 (.in_1(in_1), .in_2(in_2[3:0]), .in_3(in_3[3:0]), .out_4(out_4[3:0]));
  QUADMUX quadmux_2 (.in_1(in_1), .in_2(in_2[7:4]), .in_3(in_3[7:4]), .out_4(out_4[7:4]));
  QUADMUX quadmux_3 (
    .in_1(in_1), .in_2({1'b0, in_2[10:8]}), .in_3({1'b0, in_3[10:8]}),
    .out_4({quadmux_3_out_4[3], out_4[10:8]}));
endmodule

module DEMUX (
  input  [4:0] in_1,
  input  in_2,
  output [4:0] out_3,
  output [4:0] out_4
);

  wire ic7404_1__2__1y;

  IC7404 ic7404_1 (
    ._1__1A(in_2), ._2__1Y(ic7404_1__2__1y));  // open: _3__2A, _4__2Y, _5__3A, _6__3Y, _7__GND, _14__Vcc, _13__6A, _12__6Y, _11__5A, _10__5Y, _9__4A, _8__4Y
  IC7408 ic7408_1 (
    ._1__1A(in_1[0]), ._2__1B(ic7404_1__2__1y), ._3__1Y(out_3[0]), ._4__2A(in_1[1]),
    ._5__2B(ic7404_1__2__1y), ._6__2Y(out_3[1]), ._13__4B(in_1[0]), ._12__4A(in_2), ._11__4Y(out_4[0]),
    ._10__3B(in_1[1]), ._9__3A(in_2), ._8__3Y(out_4[1]));  // open: _7__GND, _14__Vcc
  IC7408 ic7408_2 (
    ._1__1A(in_1[2]), ._2__1B(ic7404_1__2__1y), ._3__1Y(out_3[2]), ._4__2A(in_1[3]),
    ._5__2B(ic7404_1__2__1y), ._6__2Y(out_3[3]), ._13__4B(in_1[2]), ._12__4A(in_2), ._11__4Y(out_4[2]),
    ._10__3B(in_1[3]), ._9__3A(in_2), ._8__3Y(out_4[3]));  // open: _7__GND, _14__Vcc
  IC7408 ic7408_3 (
    ._1__1A(in_1[4]), ._2__1B(ic7404_1__2__1y), ._3__1Y(out_3[4]), ._13__4B(in_1[4]), ._12__4A(in_2),
    ._11__4Y(out_4[4]));  // open: _4__2A, _5__2B, _6__2Y, _7__GND, _14__Vcc, _10__3B, _9__3A, _8__3Y
endmodule

module ICAND (
  input  [3:0] in_1,
  input  [3:0] in_2,
  output [3:0] out_3
);

  IC7408 ic7408_1 (
    ._1__1A(in_1[0]), ._2__1B(in_2[0]), ._3__1Y(out_3[0]), ._4__2A(in_1[1]), ._5__2B(in_2[1]),
    ._6__2Y(out_3[1]), ._13__4B(in_1[2]), ._12__4A(in_2[2]), ._11__4Y(out_3[2]), ._10__3B(in_1[3]),
    ._9__3A(in_2[3]), ._8__3Y(out_3[3]));  // open: _7__GND, _14__Vcc
endmodule

module _32AND (
  input  [31:0] in_1,
  input  [31:0] in_2,
  output [31:0] out_3
);

  ICAND icand_1 (.in_1(in_1[3:0]), .in_2(in_2[3:0]), .out_3(out_3[3:0]));
  ICAND icand_2 (.in_1(in_1[7:4]), .in_2(in_2[7:4]), .out_3(out_3[7:4]));
  ICAND icand_3 (.in_1(in_1[11:8]), .in_2(in_2[11:8]), .out_3(out_3[11:8]));
  ICAND icand_4 (.in_1(in_1[15:12]), .in_2(in_2[15:12]), .out_3(out_3[15:12]));
  ICAND icand_5 (.in_1(in_1[19:16]), .in_2(in_2[19:16]), .out_3(out_3[19:16]));
  ICAND icand_6 (.in_1(in_1[23:20]), .in_2(in_2[23:20]), .out_3(out_3[23:20]));
  ICAND icand_7 (.in_1(in_1[27:24]), .in_2(in_2[27:24]), .out_3(out_3[27:24]));
  ICAND icand_8 (.in_1(in_1[31:28]), .in_2(in_2[31:28]), .out_3(out_3[31:28]));
endmodule

module firstShift (
  input  [31:0] in_1,
  input  [10:0] in_2,
  output [31:0] out_3,
  output [10:0] out_4,
  output out_5,
  output out_6
);

  wire bitfinder_1_found, subtractor_2_bout;
  wire [4:0] bit_extender_5_out, bitfinder_1_index, negator_1_out;
  wire [31:0] adder_1_out, bit_extender_1_out, bit_extender_2_out, bit_extender_3_out,
       n32bitconverter_1_out_2, n32bitmux_1_out_4, n32bitmux_2_out_4, n32bitmux_3_out_4, negator_2_out,
       shifter_1_out, shifter_2_out, subtractor_1_out, subtractor_2_out;

  assign bit_extender_1_out = {{21{1'b0}}, in_2};  // Bit_Extender bit_extender_1
  BitFinder #(.width(32), .\type ("high1")) bitfinder_1 (
    .in(in_1), .index(bitfinder_1_index), .found(bitfinder_1_found));
  Negator #(.width(5)) negator_1 (.in(bitfinder_1_index), .out(negator_1_out));
  Adder #(.width(32)) adder_1 (.a(bit_extender_1_out), .b(n32bitmux_3_out_4), .out(adder_1_out));  // open: cin, cout
  Subtractor #(.width(32)) subtractor_1 (
    .a(bit_extender_1_out), .b(n32bitmux_3_out_4), .out(subtractor_1_out));  // open: bin, bout
  assign bit_extender_2_out = {{27{1'b0}}, negator_1_out};  // Bit_Extender bit_extender_2
  assign bit_extender_3_out = {{28{1'b0}}, 4'b1001};  // Bit_Extender bit_extender_3
  _32bitMUX u_32bitmux_1 (
    .in_1(subtractor_2_bout), .in_2(subtractor_1_out), .in_3(adder_1_out), .out_4(n32bitmux_1_out_4));
  _32bitConverter u_32bitconverter_1 (.in_1(1'b0), .out_2(n32bitconverter_1_out_2));
  Subtractor #(.width(32)) subtractor_2 (
    .a(bit_extender_2_out), .b(bit_extender_3_out), .out(subtractor_2_out), .bout(subtractor_2_bout));  // open: bin
  _32bitMUX u_32bitmux_2 (
    .in_1(bitfinder_1_found), .in_2(n32bitconverter_1_out_2), .in_3(n32bitmux_1_out_4),
    .out_4({n32bitmux_2_out_4[31:13], out_6, out_5, n32bitmux_2_out_4[10:0]}));
  Negator #(.width(32)) negator_2 (.in(subtractor_2_out), .out(negator_2_out));
  Shifter #(.width(32), .shift("lr")) shifter_1 (.in(in_1), .\dist (bit_extender_5_out), .out(shifter_1_out));
  Shifter #(.width(32)) shifter_2 (.in(in_1), .\dist (bit_extender_5_out), .out(shifter_2_out));
  Bit_Extender #(.in_width(32), .out_width(11)) bit_extender_4 (
    .in({n32bitmux_2_out_4[31:13], out_6, out_5, n32bitmux_2_out_4[10:0]}), .out(out_4));
  _32bitMUX u_32bitmux_3 (
    .in_1(subtractor_2_bout), .in_2(subtractor_2_out), .in_3(negator_2_out), .out_4(n32bitmux_3_out_4));
  Bit_Extender #(.in_width(32), .out_width(5)) bit_extender_5 (.in(n32bitmux_3_out_4), .out(bit_extender_5_out));
  _32bitMUX u_32bitmux_4 (.in_1(subtractor_2_bout), .in_2(shifter_2_out), .in_3(shifter_1_out), .out_4(out_3));

  // Notes on the sheet:
  //   32 ADD
  //   32 sub
  //   sub
  //   32 mux
  //   32 mux
endmodule

module Rounding (
  input  [31:0] \input ,
  output [31:0] out_2
);

  wire ic7404_1__2__1y, ic7404_1__4__2y, ic7408_1__3__1y, ic7408_1__6__2y, ic7408_1__8__3y, ic7408_1__11__4y,
       ic7432_1__3__1y, ic7432_1__11__4y;
  wire [31:0] bit_extender_1_out;

  IC7404 ic7404_1 (
    ._1__1A(\input [0]), ._2__1Y(ic7404_1__2__1y), ._3__2A(\input [1]), ._4__2Y(ic7404_1__4__2y));  // open: _5__3A, _6__3Y, _7__GND, _14__Vcc, _13__6A, _12__6Y, _11__5A, _10__5Y, _9__4A, _8__4Y
  Adder #(.width(32)) adder_1 (.a(bit_extender_1_out), .b({3'b000, \input [31:3]}), .out(out_2));  // open: cin, cout
  IC7432 ic7432_1 (
    ._1__1A(\input [0]), ._2__1B(\input [1]), ._3__1Y(ic7432_1__3__1y), ._13__4B(ic7408_1__3__1y),
    ._12__4A(ic7408_1__11__4y), ._11__4Y(ic7432_1__11__4y));  // open: _4__2A, _5__2B, _6__2Y, _7__GND, _14__Vcc, _10__3B, _9__3A, _8__3Y
  assign bit_extender_1_out = {{31{1'b0}}, ic7432_1__11__4y};  // Bit_Extender bit_extender_1
  IC7408 ic7408_1 (
    ._1__1A(ic7432_1__3__1y), ._2__1B(\input [2]), ._3__1Y(ic7408_1__3__1y), ._4__2A(ic7404_1__2__1y),
    ._5__2B(ic7404_1__4__2y), ._6__2Y(ic7408_1__6__2y), ._13__4B(\input [3]), ._12__4A(ic7408_1__8__3y),
    ._11__4Y(ic7408_1__11__4y), ._10__3B(\input [2]), ._9__3A(ic7408_1__6__2y), ._8__3Y(ic7408_1__8__3y));  // open: _7__GND, _14__Vcc

  // Notes on the sheet:
  //   not
  //   or
  //   adder 32
  //   and
endmodule

module AfterShift (
  input  [31:0] in_1,
  input  [10:0] in_2,
  input  in_3,
  input  in_4,
  output [31:0] out_5,
  output [10:0] out_6,
  output out_7,
  output out_8
);

  wire bitfinder_1_found, subtractor_2_bout;
  wire [4:0] bit_extender_5_out, bitfinder_1_index, negator_1_out;
  wire [31:0] adder_1_out, bit_extender_1_out, bit_extender_2_out, bit_extender_3_out, n32bitmux_1_out_4,
       n32bitmux_2_out_4, n32bitmux_3_out_4, negator_2_out, shifter_1_out, shifter_2_out, subtractor_1_out,
       subtractor_2_out;

  assign bit_extender_1_out = {{19{1'b0}}, {in_4, in_3, in_2}};  // Bit_Extender bit_extender_1
  BitFinder #(.width(32), .\type ("high1")) bitfinder_1 (
    .in(in_1), .index(bitfinder_1_index), .found(bitfinder_1_found));
  Adder #(.width(32)) adder_1 (.a(bit_extender_1_out), .b(n32bitmux_3_out_4), .out(adder_1_out));  // open: cin, cout
  Subtractor #(.width(32)) subtractor_1 (
    .a(bit_extender_1_out), .b(n32bitmux_3_out_4), .out(subtractor_1_out));  // open: bin, bout
  Negator #(.width(5)) negator_1 (.in(bitfinder_1_index), .out(negator_1_out));
  assign bit_extender_2_out = {{27{1'b0}}, negator_1_out};  // Bit_Extender bit_extender_2
  assign bit_extender_3_out = {{28{1'b0}}, 4'b1100};  // Bit_Extender bit_extender_3
  _32bitMUX u_32bitmux_1 (
    .in_1(subtractor_2_bout), .in_2(subtractor_1_out), .in_3(adder_1_out), .out_4(n32bitmux_1_out_4));
  Subtractor #(.width(32)) subtractor_2 (
    .a(bit_extender_2_out), .b(bit_extender_3_out), .out(subtractor_2_out), .bout(subtractor_2_bout));  // open: bin
  _32bitMUX u_32bitmux_2 (
    .in_1(bitfinder_1_found), .in_2(bit_extender_1_out), .in_3(n32bitmux_1_out_4),
    .out_4({n32bitmux_2_out_4[31:13], out_8, n32bitmux_2_out_4[11:0]}));
  Negator #(.width(32)) negator_2 (.in(subtractor_2_out), .out(negator_2_out));
  Shifter #(.width(32), .shift("lr")) shifter_1 (.in(in_1), .\dist (bit_extender_5_out), .out(shifter_1_out));
  Shifter #(.width(32)) shifter_2 (.in(in_1), .\dist (bit_extender_5_out), .out(shifter_2_out));
  _32bitMUX u_32bitmux_3 (
    .in_1(subtractor_2_bout), .in_2(subtractor_2_out), .in_3(negator_2_out), .out_4(n32bitmux_3_out_4));
  Bit_Extender #(.in_width(32), .out_width(11)) bit_extender_4 (
    .in({n32bitmux_2_out_4[31:13], out_8, n32bitmux_2_out_4[11:0]}), .out(out_6));
  Bit_Extender #(.in_width(32), .out_width(5)) bit_extender_5 (.in(n32bitmux_3_out_4), .out(bit_extender_5_out));
  _32bitMUX u_32bitmux_4 (.in_1(subtractor_2_bout), .in_2(shifter_2_out), .in_3(shifter_1_out), .out_4(out_5));
  IC7486 ic7486_1 (
    ._1__1A(out_8), ._2__1B(n32bitmux_2_out_4[11]), ._3__1Y(out_7));  // open: _4__2A, _5__2B, _6__2Y, _7__GND, _14__Vcc, _13__4B, _12__4A, _11__4Y, _10__3B, _9__3A, _8__3Y

  // Notes on the sheet:
  //   finding the highest 1 bit
  //   32 ADD
  //   32 sub
  //   sub
  //   32 mux
  //   32 mux
endmodule

module _32bitConverter (
  input  in_1,
  output [31:0] out_2
);


  assign out_2 = {32{in_1}};
endmodule

module IC7404 (
  input  _1__1A,
  input  _14__Vcc,
  input  _13__6A,
  input  _3__2A,
  input  _11__5A,
  input  _5__3A,
  input  _9__4A,
  input  _7__GND,
  output _2__1Y,
  output _12__6Y,
  output _4__2Y,
  output _10__5Y,
  output _6__3Y,
  output _8__4Y
);

  not not_1 (_2__1Y, _1__1A);
  not not_2 (_4__2Y, _3__2A);
  not not_3 (_6__3Y, _5__3A);
  not not_4 (_12__6Y, _13__6A);
  not not_5 (_10__5Y, _11__5A);
  not not_6 (_8__4Y, _9__4A);

  // Notes on the sheet:
  //   7407: hex inverter
endmodule

module IC7408 (
  input  _1__1A,
  input  _14__Vcc,
  input  _2__1B,
  input  _13__4B,
  input  _12__4A,
  input  _4__2A,
  input  _5__2B,
  input  _10__3B,
  input  _9__3A,
  input  _7__GND,
  output _3__1Y,
  output _11__4Y,
  output _6__2Y,
  output _8__3Y
);

  and and_1 (_3__1Y, _2__1B, _1__1A);
  and and_2 (_6__2Y, _5__2B, _4__2A);
  and and_3 (_11__4Y, _13__4B, _12__4A);
  and and_4 (_8__3Y, _10__3B, _9__3A);

  // Notes on the sheet:
  //   7408: quad AND
endmodule

module IC7432 (
  input  _1__1A,
  input  _14__Vcc,
  input  _2__1B,
  input  _13__4B,
  input  _12__4A,
  input  _4__2A,
  input  _5__2B,
  input  _10__3B,
  input  _9__3A,
  input  _7__GND,
  output _3__1Y,
  output _11__4Y,
  output _6__2Y,
  output _8__3Y
);

  or or_1 (_3__1Y, _2__1B, _1__1A);
  or or_2 (_6__2Y, _5__2B, _4__2A);
  or or_3 (_11__4Y, _13__4B, _12__4A);
  or or_4 (_8__3Y, _10__3B, _9__3A);

  // Notes on the sheet:
  //   7432: quad OR
endmodule

module IC74157 (
  input  _1__S,
  input  _16__Vcc,
  input  _2__A1,
  input  _15__G,
  input  _3__B1,
  input  _14__A4,
  input  _13__B4,
  input  _5__A2,
  input  _6__B2,
  input  _11__A3,
  input  _10__B3,
  input  _8__GND,
  output _4__Y1,
  output _12__Y4,
  output _7__Y2,
  output _9__Y3
);

  wire multiplexer_1_out, multiplexer_2_out, multiplexer_3_out, multiplexer_4_out, not_1_out;

  Multiplexer #(.enable("false")) multiplexer_1 (.in0(_2__A1), .in1(_3__B1), .out(multiplexer_1_out), .sel(_1__S));
  and and_1 (_4__Y1, multiplexer_1_out, not_1_out);
  Multiplexer #(.enable("false")) multiplexer_2 (.in0(_5__A2), .in1(_6__B2), .out(multiplexer_2_out), .sel(_1__S));
  and and_2 (_7__Y2, multiplexer_2_out, not_1_out);
  not not_1 (not_1_out, _15__G);
  Multiplexer #(.enable("false")) multiplexer_3 (.in0(_14__A4), .in1(_13__B4), .out(multiplexer_3_out), .sel(_1__S));
  and and_3 (_12__Y4, multiplexer_3_out, not_1_out);
  Multiplexer #(.enable("false")) multiplexer_4 (.in0(_11__A3), .in1(_10__B3), .out(multiplexer_4_out), .sel(_1__S));
  and and_4 (_9__Y3, multiplexer_4_out, not_1_out);

  // Notes on the sheet:
  //   74157: Quad 2-Line to 1-Line Multiplexer
endmodule

module IC7486 (
  input  _1__1A,
  input  _14__Vcc,
  input  _2__1B,
  input  _13__4B,
  input  _12__4A,
  input  _4__2A,
  input  _5__2B,
  input  _10__3B,
  input  _9__3A,
  input  _7__GND,
  output _3__1Y,
  output _11__4Y,
  output _6__2Y,
  output _8__3Y
);

  xor xor_1 (_3__1Y, _2__1B, _1__1A);
  xor xor_2 (_6__2Y, _5__2B, _4__2A);
  xor xor_3 (_11__4Y, _13__4B, _12__4A);
  xor xor_4 (_8__3Y, _10__3B, _9__3A);

  // Notes on the sheet:
  //   7486: quad XOR
endmodule
